# Fritzing sketch lock_circuit (saved by Fritzing 0.9.3b)
breadboards: 1

parts:
  Part1 = Arduino MKR WiFi 1010
  S1 = Reed switch [package=THT]
  R1 = Resistor [package="2010 [SMD]"]
  J1 = Basic Servo

nets:
  N1: Part1.D12_SCL, S1.pin_1, R1.Pin_1
  GND: Part1.GND, R1.Pin_0, J1.gnd
  5V: Part1.5V, S1.pin_2, J1.vcc

custom parts:
  Arduino MKR WiFi 1010: This is the newest version of the MKR 1000 WIFI, but with an ESP32 module on board made by U-BLOX.
  Resistor: Resistor Basic schematic elements and footprints for 0603, 1206, and PTH resistors.
